// Logisim project rsh44_lab7.circ as structural Verilog: 3 circuits, main circuit main
module main (
  input  [7:0] ALU_A,
  input  [7:0] ALU_B,
  input  [2:0] ALU_Op,
  input  [7:0] REG_rd,
  input  [2:0] rd,
  input  Reg_WE,
  input  [2:0] rs,
  input  [2:0] rt
);

  wire CLK, clock_1_out, tick_out;
  wire [7:0] ALU_Out, REG_rs, REG_rt;

  Clock clock_1 (.out(clock_1_out));
  or or_1 (CLK, clock_1_out, tick_out);
  Button tick (.out(tick_out));
  // Probe on ALU_A
  // Probe on ALU_B
  // Probe on ALU_Out
  // Probe on REG_rd
  // Probe on REG_rs
  // Probe on REG_rt
  ALU alu_1 (.A(ALU_A), .B(ALU_B), .ALU_Op(ALU_Op), .ALU_Out(ALU_Out));
  // Register_File register_file_1: pin names not known; wires that end beside it: CLK, rs, rt, rd, Reg_WE, REG_rd, REG_rs, REG_rt

  // Notes on the sheet:
  //   ALU component
  //   Reg File component
endmodule

module ALU (
  input  [7:0] A,
  input  [7:0] B,
  input  [2:0] ALU_Op,
  output [7:0] ALU_Out
);

  wire [2:0] bit_extender_1_out, bit_extender_2_out;
  wire [7:0] adder_1_out, and_1_out, not_1_p2, or_1_out, shifter_1_out, shifter_2_out, subtractor_1_out,
       undriven, xor_1_out;

  Bit_Extender #(.out_width(3)) bit_extender_1 (.in(B), .out(bit_extender_1_out));
  Bit_Extender #(.out_width(3)) bit_extender_2 (.in(B), .out(bit_extender_2_out));
  Adder adder_1 (.a(A), .b(B), .out(adder_1_out));  // open: cin, cout
  Subtractor subtractor_1 (.a(A), .b(B), .out(subtractor_1_out));  // open: bin, bout
  assign and_1_out = A & B;  // AND_Gate and_1, 8 bits wide
  assign or_1_out = A | B | undriven;  // OR_Gate or_1, 8 bits wide
  ExactlyOne xor_1[7:0] (.out(xor_1_out), .in0(undriven), .in1(A), .in3(B));
  // NOT_Gate #(.width(8)) not_1: pin names not known; wires that end beside it: B, not_1_p2
  Shifter shifter_1 (.in(A), .\dist (bit_extender_1_out), .out(shifter_1_out));
  Shifter #(.shift("lr")) shifter_2 (.in(A), .\dist (bit_extender_2_out), .out(shifter_2_out));
  Multiplexer #(.select(3), .width(8)) multiplexer_1 (
    .in0(adder_1_out), .in1(subtractor_1_out), .in2(and_1_out), .in3(or_1_out), .in4(xor_1_out),
    .in5(not_1_p2), .in6(shifter_1_out), .in7(shifter_2_out), .out(ALU_Out), .sel(ALU_Op));  // open: en
endmodule

module Register_File (
  input  CLK,
  input  [2:0] rs,
  input  [2:0] rt,
  input  [2:0] rd,
  input  [7:0] REG_rd,
  input  Reg_WE,
  output [7:0] REG_rs,
  output [7:0] REG_rt
);

  wire demultiplexer_1_out1, demultiplexer_1_out2, demultiplexer_1_out3, demultiplexer_1_out4,
       demultiplexer_1_out5, demultiplexer_1_out6, demultiplexer_1_out7;
  wire [7:0] _1_q, _2_q, _3_q, _4_q, _5_q, _6_q, _7_q;

  Demultiplexer #(.select(3)) demultiplexer_1 (
    .out1(demultiplexer_1_out1), .out2(demultiplexer_1_out2), .out3(demultiplexer_1_out3),
    .out4(demultiplexer_1_out4), .out5(demultiplexer_1_out5), .out6(demultiplexer_1_out6),
    .out7(demultiplexer_1_out7), .in(Reg_WE), .sel(rd));  // open: out0, en
  Register _1 (.D(REG_rd), .en(demultiplexer_1_out1), .Q(_1_q), .clk(CLK));  // open: clr
  Register _2 (.D(REG_rd), .en(demultiplexer_1_out2), .Q(_2_q), .clk(CLK));  // open: clr
  Register _3 (.D(REG_rd), .en(demultiplexer_1_out3), .Q(_3_q), .clk(CLK));  // open: clr
  Register _4 (.D(REG_rd), .en(demultiplexer_1_out4), .Q(_4_q), .clk(CLK));  // open: clr
  Register _5 (.D(REG_rd), .en(demultiplexer_1_out5), .Q(_5_q), .clk(CLK));  // open: clr
  Register _6 (.D(REG_rd), .en(demultiplexer_1_out6), .Q(_6_q), .clk(CLK));  // open: clr
  Register _7 (.D(REG_rd), .en(demultiplexer_1_out7), .Q(_7_q), .clk(CLK));  // open: clr
  Multiplexer #(.select(3), .width(8)) multiplexer_1 (
    .in0({8{1'b0}}), .in1(_1_q), .in2(_2_q), .in3(_3_q), .in4(_4_q), .in5(_5_q), .in6(_6_q), .in7(_7_q),
    .out(REG_rs), .sel(rs));  // open: en
  Multiplexer #(.select(3), .width(8)) multiplexer_2 (
    .in0({8{1'b0}}), .in1(_1_q), .in2(_2_q), .in3(_3_q), .in4(_4_q), .in5(_5_q), .in6(_6_q), .in7(_7_q),
    .out(REG_rt), .sel(rt));  // open: en
endmodule
