// Logisim project rsh44_lab8.circ as structural Verilog: 1 circuit, main circuit main
module main (
);

  wire button_1_out, CLK, clock_1_out, comparator_1_eq;
  wire [1:0] Inst;
  wire [3:0] ACC, adder_1_out, adder_2_out, DISP_q, multiplexer_1_out, register_1_q, subtractor_1_out;

  Clock clock_1 (.out(clock_1_out));
  Button button_1 (.out(button_1_out));
  or or_1 (CLK, clock_1_out, button_1_out);
  Adder #(.width(4)) adder_1 (.a(register_1_q), .b(4'b0001), .out(adder_1_out));  // open: cin, cout
  Adder #(.width(4)) adder_2 (.a(ACC), .b(4'b0001), .out(adder_2_out));  // open: cin, cout
  Subtractor #(.width(4)) subtractor_1 (.a(ACC), .b(4'b0001), .out(subtractor_1_out));  // open: bin, bout
  Register #(.width(4)) register_1 (.D(adder_1_out), .Q(register_1_q), .clk(CLK));  // open: en, clr
  Register #(.width(4)) u_ACC (.D(multiplexer_1_out), .Q(ACC), .clk(CLK));  // open: en, clr
  Multiplexer #(.select(2), .width(4)) multiplexer_1 (
    .in0(4'b0000), .in1(adder_2_out), .in2(subtractor_1_out), .in3(ACC), .out(multiplexer_1_out), .sel(Inst));  // open: en
  // Probe on Inst
  ROM #(.addrWidth(4), .dataWidth(2)) rom_1 (.addr(register_1_q), .data(Inst));  // open: sel
  Comparator #(.width(2)) comparator_1 (.a(Inst), .b(2'b11), .eq(comparator_1_eq));  // open: gt, lt
  Hex_Digit_Display hex_digit_display_1 (.value(DISP_q));  // open: dp
  Register #(.width(4)) DISP (.D(ACC), .en(comparator_1_eq), .Q(DISP_q), .clk(CLK));  // open: clr

  // Notes on the sheet:
  //   instructions
  //   0: ACC = 0
  //   1: ACC = ACC + 1
  //   2: ACC = ACC - 1
  //   3: DISP = ACC, ACC = ACC
  //   contents of rom_1 (hex, n*v repeats v):
  //   0 5*1 3 2 2 3 4*1 3 2
endmodule
