// Logisim project rsh44_proj2.circ as structural Verilog: 6 circuits, main circuit main
module main (
);

  wire ALUB, and_1_out, and_2_out, and_3_out, and_4_out, beq, bge, blt, bne, branch, button_1_out, CLK,
       clock_1_out, halt, isJump, jr, not_1_out, or_2_out, put, Reg_WE, RS__RT, RS_RT, RS_RT_t, store;
  wire [2:0] ALUOp, rd, RegDataSrc, rs, rt;
  wire [3:0] Display_digit0, Display_digit1, Display_digit2, Display_digit3;
  wire [7:0] ALUOut, imm, multiplexer_1_out, multiplexer_2_out, multiplexer_3_out, PC_1, PC_FSM_pc_out,
       RAMOut, REG_rs, REG_rt;
  wire [21:0] rom_1_data;

  Multiplexer #(.width(8)) multiplexer_1 (.in0(imm), .in1(REG_rs), .out(multiplexer_1_out), .sel(jr));  // open: en
  Comparator comparator_1 (.a(REG_rs), .b(REG_rt), .gt(RS_RT_t), .eq(RS__RT), .lt(RS_RT));
  Clock clock_1 (.out(clock_1_out));
  Button button_1 (.out(button_1_out));
  // Probe on PC_FSM_pc_out
  PC_FSM PC_FSM (
    .Offset(imm), .Target(multiplexer_1_out), .Branch(branch), .Jump(isJump), .Halt(halt), .CLK(CLK),
    .PC_Out(PC_FSM_pc_out), .PC_1_Out(PC_1));
  or or_1 (CLK, clock_1_out, button_1_out);
  Display Display (
    .Data_Lo(REG_rt), .Data_Hi(REG_rs), .Write_Enable(put), .CLK(CLK), .Digit0(Display_digit0),
    .Digit1(Display_digit1), .Digit2(Display_digit2), .Digit3(Display_digit3));
  Control Control (
    .Instruction(rom_1_data), .imm(imm), .rs(rs), .rt(rt), .rd(rd), .halt(halt), .Put(put), .Reg_WE(Reg_WE),
    .RegDataSrc(RegDataSrc), .ALUOp(ALUOp), .Store(store), .ALUB(ALUB), .blt(blt), .bge(bge), .beq(beq),
    .bne(bne), .isJump(isJump), .jr(jr));
  ROM #(.dataWidth(22)) rom_1 (.addr(PC_FSM_pc_out), .data(rom_1_data));  // open: sel
  RAM #(.bus("separate")) ram_1 (
    .addr(ALUOut), .din(REG_rt), .data(RAMOut), .str(store), .clk(CLK));  // open: sel, ld, clr
  and and_1 (and_1_out, blt, RS_RT);
  and and_2 (and_2_out, bge, or_2_out);
  or or_2 (or_2_out, RS__RT, RS_RT_t);
  and and_3 (and_3_out, beq, RS__RT);
  and and_4 (and_4_out, bne, not_1_out);
  // NOT_Gate not_1 has open pins: in=open, out=not_1_out
  Hex_Digit_Display hex_digit_display_1 (.value(Display_digit3));  // open: dp
  Hex_Digit_Display hex_digit_display_2 (.value(Display_digit2));  // open: dp
  or or_3 (branch, and_1_out, and_2_out, and_3_out, and_4_out);
  Hex_Digit_Display hex_digit_display_3 (.value(Display_digit1));  // open: dp
  Hex_Digit_Display hex_digit_display_4 (.value(Display_digit0));  // open: dp
  LED u_HALT (.in(halt));
  Multiplexer #(.select(3), .width(8)) multiplexer_2 (
    .in0(ALUOut), .in1(imm), .in2(REG_rs), .in3(RAMOut), .in4(PC_1), .out(multiplexer_2_out), .sel(RegDataSrc));  // open: in5, in6, in7, en
  Multiplexer #(.width(8)) multiplexer_3 (.in0(imm), .in1(REG_rt), .out(multiplexer_3_out), .sel(ALUB));  // open: en
  Register_File Register_File (
    .CLK(CLK), .rs(rs), .rt(rt), .rd(rd), .REG_rd(multiplexer_2_out), .Reg_WE(Reg_WE), .REG_rs(REG_rs),
    .REG_rt(REG_rt));
  ALU ALU (.A(REG_rs), .B(multiplexer_3_out), .Operation(ALUOp), .Result(ALUOut));

  // Notes on the sheet:
  //   ROM
  //   RAM
  //   contents of rom_1 (hex, n*v repeats v):
  //   60600 4010a 2c0705 24000 0 bf000 1c3601 1e0a01 341009 a7000 1c3601 1e0901 2c0705 1e3601 83200 c8900
  //   2a0012 40101 1e3601 83700 2e3800
endmodule

module ALU (
  input  [7:0] A,
  input  [7:0] B,
  input  [2:0] Operation,
  output [7:0] Result
);

  wire [2:0] bit_extender_1_out, bit_extender_2_out;
  wire [7:0] adder_1_out, and_1_out, not_1_p2, or_1_out, shifter_1_out, shifter_2_out, subtractor_1_out,
       undriven, undriven_2, xor_1_out;

  Bit_Extender #(.out_width(3)) bit_extender_1 (.in(B), .out(bit_extender_1_out));
  Bit_Extender #(.out_width(3)) bit_extender_2 (.in(B), .out(bit_extender_2_out));
  Adder adder_1 (.a(A), .b(B), .out(adder_1_out));  // open: cin, cout
  Subtractor subtractor_1 (.a(A), .b(B), .out(subtractor_1_out));  // open: bin, bout
  assign and_1_out = A & B & undriven;  // AND_Gate and_1, 8 bits wide
  assign or_1_out = undriven | A | B | undriven_2;  // OR_Gate or_1, 8 bits wide
  ExactlyOne xor_1[7:0] (.out(xor_1_out), .in0(undriven_2), .in1(A), .in3(B));
  // NOT_Gate #(.width(8)) not_1: pin names not known; wires that end beside it: B, not_1_p2
  Shifter shifter_1 (.in(A), .\dist (bit_extender_1_out), .out(shifter_1_out));
  Shifter #(.shift("lr")) shifter_2 (.in(A), .\dist (bit_extender_2_out), .out(shifter_2_out));
  Multiplexer #(.select(3), .width(8)) multiplexer_1 (
    .in0(adder_1_out), .in1(subtractor_1_out), .in2(and_1_out), .in3(or_1_out), .in4(xor_1_out),
    .in5(not_1_p2), .in6(shifter_1_out), .in7(shifter_2_out), .out(Result), .sel(Operation));  // open: en
endmodule

module Register_File (
  input  CLK,
  input  [2:0] rs,
  input  [2:0] rt,
  input  [2:0] rd,
  input  [7:0] REG_rd,
  input  Reg_WE,
  output [7:0] REG_rs,
  output [7:0] REG_rt
);

  wire demultiplexer_1_out1, demultiplexer_1_out2, demultiplexer_1_out3, demultiplexer_1_out4,
       demultiplexer_1_out5, demultiplexer_1_out6, demultiplexer_1_out7;
  wire [7:0] _1_q, _2_q, _3_q, _4_q, _5_q, _6_q, _7_q;

  Demultiplexer #(.select(3)) demultiplexer_1 (
    .out1(demultiplexer_1_out1), .out2(demultiplexer_1_out2), .out3(demultiplexer_1_out3),
    .out4(demultiplexer_1_out4), .out5(demultiplexer_1_out5), .out6(demultiplexer_1_out6),
    .out7(demultiplexer_1_out7), .in(Reg_WE), .sel(rd));  // open: out0, en
  Register _1 (.D(REG_rd), .en(demultiplexer_1_out1), .Q(_1_q), .clk(CLK));  // open: clr
  Register _3 (.D(REG_rd), .en(demultiplexer_1_out3), .Q(_3_q), .clk(CLK));  // open: clr
  Register _5 (.D(REG_rd), .en(demultiplexer_1_out5), .Q(_5_q), .clk(CLK));  // open: clr
  Register _7 (.D(REG_rd), .en(demultiplexer_1_out7), .Q(_7_q), .clk(CLK));  // open: clr
  Register _2 (.D(REG_rd), .en(demultiplexer_1_out2), .Q(_2_q), .clk(CLK));  // open: clr
  Register _4 (.D(REG_rd), .en(demultiplexer_1_out4), .Q(_4_q), .clk(CLK));  // open: clr
  Register _6 (.D(REG_rd), .en(demultiplexer_1_out6), .Q(_6_q), .clk(CLK));  // open: clr
  Multiplexer #(.select(3), .width(8)) multiplexer_1 (
    .in0({8{1'b0}}), .in1(_1_q), .in2(_2_q), .in3(_3_q), .in4(_4_q), .in5(_5_q), .in6(_6_q), .in7(_7_q),
    .out(REG_rs), .sel(rs));  // open: en
  Multiplexer #(.select(3), .width(8)) multiplexer_2 (
    .in0({8{1'b0}}), .in1(_1_q), .in2(_2_q), .in3(_3_q), .in4(_4_q), .in5(_5_q), .in6(_6_q), .in7(_7_q),
    .out(REG_rt), .sel(rt));  // open: en
endmodule

module PC_FSM (
  input  [7:0] Offset,
  input  [7:0] Target,
  input  Branch,
  input  Jump,
  input  Halt,
  input  CLK,
  output [7:0] PC_Out,
  output [7:0] PC_1_Out
);

  wire not_1_out;
  wire [7:0] multiplexer_1_out, multiplexer_2_out;

  Adder adder_1 (.a(PC_Out), .b(multiplexer_1_out), .out(PC_1_Out));  // open: cin, cout
  Multiplexer #(.width(8)) multiplexer_1 (.in0(8'h1), .in1(Offset), .out(multiplexer_1_out), .sel(Branch));  // open: en
  Multiplexer #(.width(8)) multiplexer_2 (
    .in0(PC_1_Out), .in1(Target), .out(multiplexer_2_out), .sel(Jump));  // open: en
  Register PC (.D(multiplexer_2_out), .en(not_1_out), .Q(PC_Out), .clk(CLK));  // open: clr
  not not_1 (not_1_out, Halt);
endmodule

module Control (
  input  [21:0] Instruction,
  output [7:0] imm,
  output [2:0] rs,
  output [2:0] rt,
  output [2:0] rd,
  output halt,
  output Put,
  output Reg_WE,
  output [2:0] RegDataSrc,
  output [2:0] ALUOp,
  output Store,
  output ALUB,
  output blt,
  output bge,
  output beq,
  output bne,
  output isJump,
  output jr
);

  wire add, adi, \and , ani, j, jal, ld, li, mov, \not , \or , or_1_out, or_2_out, or_3_out, or_4_out,
       or_5_out, or_6_out, ori, sbi, shl, shr, sli, sri, sub, undriven, undriven_2, \xor , xri;

  or or_1 (or_1_out, sub, sbi);
  buf or_2 (or_2_out, undriven);  // OR_Gate
  buf or_3 (or_3_out, undriven);  // OR_Gate
  or or_4 (or_4_out, \xor , xri);
  or or_5 (or_5_out, shl, sli, undriven_2);
  or or_6 (or_6_out, undriven_2, shr, sri);
  or or_7 (Reg_WE, mov, li, ld, add, \or , \xor , \not , shl, shr, adi, sbi, ani, ori, xri, sli, \and , sri, jal, sub);
  Priority_Encoder priority_encoder_1 (
    .in0(1'b1), .in1(li), .in2(mov), .in3(ld), .in4(jal), .out(RegDataSrc));  // open: in5, in6, in7, en_in, gs, en_out
  Priority_Encoder priority_encoder_2 (
    .in0(1'b1), .in1(or_1_out), .in2(or_2_out), .in3(or_3_out), .in4(or_4_out), .in5(\not ), .in6(or_5_out),
    .in7(or_6_out), .out(ALUOp));  // open: en_in, gs, en_out
  // Decoder #(.select(5)) decoder_1: pin names not known; wires that end beside it: Instruction[21:17], halt, Put, li, mov, ld, Store, add, sub, \and , \or , \xor , \not , shl, shr, adi, sbi, ani, ori, xri, sli, sri, j, jal, jr, blt, bge, beq, bne
  or or_8 (ALUB, add, sub, \and , \or , \xor , \not , shl, shr);
  or or_9 (isJump, j, jal, jr);

  assign imm = Instruction[7:0];
  assign rd = Instruction[10:8];
  assign rs = Instruction[13:11];
  assign rt = Instruction[16:14];

  // Other names for the same wires on the sheet: hlt = halt; st = Store
endmodule

module Display (
  input  [7:0] Data_Lo,
  input  [7:0] Data_Hi,
  input  Write_Enable,
  input  CLK,
  output [3:0] Digit0,
  output [3:0] Digit1,
  output [3:0] Digit2,
  output [3:0] Digit3
);

  Register #(.width(16)) register_1 (
    .D({Data_Hi, Data_Lo}), .en(Write_Enable), .Q({Digit3, Digit2, Digit1, Digit0}), .clk(CLK));  // open: clr
endmodule
