// Logisim project rsh_lab5.circ as structural Verilog: 1 circuit, main circuit main
module main (
  input  [3:0] A,
  input  [3:0] B,
  input  sub
);

  wire adder_1_cout, and_1_out, and_2_out, not_2_out, not_3_out, not_4_out, SOV, UOV;
  wire [3:0] MUX_Out, not_1_out, O;

  assign not_1_out = ~B;  // NOT_Gate not_1, 4 bits wide
  Multiplexer #(.width(4)) multiplexer_1 (.in0(B), .in1(not_1_out), .out(MUX_Out), .sel(sub));  // open: en
  // Probe on A
  // Probe on B
  // Probe on O
  LED led_1 (.in(UOV));
  Adder #(.width(4)) adder_1 (.a(A), .b(MUX_Out), .out(O), .cin(sub), .cout(adder_1_cout));
  or or_1 (SOV, and_1_out, and_1_out, and_2_out);
  // Probe on A
  // Probe on B
  // Probe on O
  LED led_2 (.in(SOV));
  xor xor_1 (UOV, sub, adder_1_cout);
  and and_1 (and_1_out, A[3], MUX_Out[3], not_2_out);
  // NOT_Gate not_2 has open pins: in=open, out=not_2_out
  // NOT_Gate not_3 has open pins: in=open, out=not_3_out
  // NOT_Gate not_4 has open pins: in=open, out=not_4_out
  and and_2 (and_2_out, not_3_out, not_4_out, O[3]);

  // Other names for the same wires on the sheet: SA = A[3]; SB = MUX_Out[3]; SO = O[3]
endmodule
